# Fritzing sketch 專題電路圖 (saved by Fritzing 0.9.3b)
breadboards: 1

parts:
  元件1 = 16-Channel 12-bit PWM Servo Driver - I2C [part_number=815]
  元件2 = Arduino Uno (Rev3)
  R1 = Resistor [tolerance=±5% resistance=220 package=THT]
  Q1 = NPN-Transistor [package="TO92 [THT]"]
  Q2 = NPN-Transistor [package="TO92 [THT]"]
  M1 = DC Motor
  D1 = Rectifier Diode [part_number=1N4001 package="300 mil [THT]"]
  CAMERA1 = TTL Serial JPEG Camera
  J1 = Basic Servo
  J2 = Basic Servo
  J3 = Basic Servo
  J4 = Basic Servo
  J5 = Basic Servo
  J6 = Basic Servo
  U1 = LM2596 step down module  # not connected
  VCC1 = Battery  # not connected

nets:
  N1: 元件1.PWM5, J6.pulse
  VCC: 元件1.5.0V, J1.vcc, J2.vcc, J3.vcc, J4.vcc, J5.vcc, J6.vcc
  GND: 元件1.GND, 元件2.GND, Q2.E, CAMERA1.GND, J1.gnd, J2.gnd, J3.gnd, J4.gnd, J5.gnd, J6.gnd
  N2: 元件1.PWM4, J5.pulse
  N3: 元件1.PWM3, J4.pulse
  N4: 元件1.PWM2, J3.pulse
  N5: 元件1.PWM1, J2.pulse
  N6: 元件1.PWM0, J1.pulse
  5V: 元件1.VCC, 元件2.5V, M1.pin_2, D1.cathode, CAMERA1.5V
  N7: 元件1.SDA, 元件2.A4/SDA
  N8: 元件1.SCL, 元件2.A5/SCL
  N9: 元件2.A0, CAMERA1.TX
  N10: 元件2.A1, CAMERA1.RX
  N11: 元件2.D4, R1.Pin_0
  N12: R1.Pin_1, Q1.B
  N13: Q1.E, Q2.B
  N14: Q1.C, Q2.C, M1.pin_1, D1.anode

notes:
  鏡頭接法是Pixetto接法
  此六顆伺服馬達接法
  黃 -> PWM
  紅 -> V+
  黑 -> GND
  18650連接LM2596時請確定是否超過5V

custom parts:
  16-Channel 12-bit PWM Servo Driver - I2C: You want to make a cool robot, maybe a hexapod walker, or maybe just a piece of art with a lot of moving parts. Or maybe you want to drive a lot of LEDs with precise PWM output. Using only two pins, control 16 free-running PWM outputs! You can even chain up 62 breakouts to control up to 992 PWM outputs.
  TTL Serial JPEG Camera: TTL Serial JPEG Camera with NTSC Out
  LM2596 step down module: LM2596 DC-DC step down power supply module 3 A.
  Battery: Your standard 2x 18650 battery pack (7,4 Volts)
